# Fritzing sketch OLTTSchematic (saved by Fritzing 0.9.3b)
breadboards: 1

parts:
  Teensy_3_1 = Teensy 3.1
  Part1 = Adafruit Thermocouple Amplifier with 1-Wire Breakout Board - MAX31850K [part_number="Adafruit #1727"]
  Part2 = Adafruit TCA9548A
  Part3 = Adafruit Thermocouple Amplifier with 1-Wire Breakout Board - MAX31850K [part_number="Adafruit #1727"]
  Part4 = Adafruit Thermocouple Amplifier with 1-Wire Breakout Board - MAX31850K [part_number="Adafruit #1727"]
  Part5 = Adafruit Thermocouple Amplifier with 1-Wire Breakout Board - MAX31850K [part_number="Adafruit #1727"]
  Part6 = Adafruit Thermocouple Amplifier with 1-Wire Breakout Board - MAX31850K [part_number="Adafruit #1727"]
  Part7 = Adafruit MPRLS Sensor Breakout [part_number=3965]
  Part8 = Adafruit MPRLS Sensor Breakout [part_number=3965]
  Part9 = Adafruit MPRLS Sensor Breakout [part_number=3965]
  R1 = Resistor [package="2512 [SMD]"]

nets:
  GND: Teensy_3_1.GND, Part1.GND, Part2.GND, Part3.GND, Part4.GND, Part5.GND, Part6.GND, Part7.GND, Part8.GND, Part9.GND
  VIN: Teensy_3_1.3V3, Part1.VIN, Part2.VCC, Part3.VIN, Part4.VIN, Part5.VIN, Part6.VIN, Part7.VIN, Part8.VIN, Part9.VIN, R1.Pin_1
  N1: Part1.DATA, Part3.DATA, Part4.DATA, Part5.DATA, Part6.DATA, R1.Pin_0
  N2: Part2.4SDA, Part7.SDA
  N3: Part2.4SCL, Part7.SCL
  N4: Part2.0SDA, Part9.SDA
  N5: Part2.0SCL, Part9.SCL
  N6: Part2.1SDA, Part8.SDA
  N7: Part2.1SCL, Part8.SCL

custom parts:
  Adafruit Thermocouple Amplifier with 1-Wire Breakout Board - MAX31850K: Thermocouples are very sensitive, requiring a good amplifier with a cold-compensation reference. So far we've carried the very nice MAX31855 which is an SPI interface thermocouple amplifier. The '855 is great but if you have a lot of thermocouples to measure it isn't terribly easy to use. That's why we are also carrying the new '850 model from Maxim - it's a "1-Wire" thermocouple amp which can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
  Adafruit TCA9548A: You just found the perfect I2C sensor, and you want to wire up two or three or more of them to your Arduino when you realize "Uh oh, this chip has a fixed I2C address, and from what I know about I2C, you cannot have two devices with the same address on the same SDA/SCL pins!" Are you out of luck? You would be, if you didn't have this ultra-cool TCA9548A 1-to-8 I2C multiplexer! Finally, a way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
  Adafruit MPRLS Sensor Breakout: This pressure sensor is special because it comes with a metal port - you can easily attach a tube to it, to measure air pressure inside a close space. In particular we think this would be a great sensor for use with making DIY assistive tech "Sip & Puff" interfaces, or measuring the pressure within a vacuum chamber or other pressurized container. The port is made of stainless steel and is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
  Resistor: Resistor Basic schematic elements and footprints for 0603, 1206, and PTH resistors.
